// Digital circuit digital_bitbakery.dig as structural Verilog
module digital_bitbakery (
  input  clk,
  input  [1:0] Distancia,
  output Serial,
  output Pwm,
  output [2:0] Pontuacao,
  output [6:0] Estado,
  output [1:0] db_Minigame,
  output db_iniciar
);

  wire Dificuldade_out, Iniciar_out, not_1_out, not_2_out, Reset_out, u_bitbakery_trigger, u_mock_hcsr04_echo;
  wire [1:0] dipswitch_1_out;
  wire [3:0] u_bitbakery_db_player_position;
  wire [6:0] B0_out, not_3_out, u_bitbakery_db_jogada;
  wire [63:0] u_bitbakery_db_map_obstacle;

  Button B0 (.out(B0_out[0]));
  Button B1 (.out(B0_out[1]));
  Button B2 (.out(B0_out[2]));
  Button B3 (.out(B0_out[3]));
  Button B4 (.out(B0_out[4]));
  Button B5 (.out(B0_out[5]));
  Button B6 (.out(B0_out[6]));
  Button Reset (.out(Reset_out));
  not not_1 (not_1_out, Reset_out);
  Button Iniciar (.out(Iniciar_out));
  not not_2 (not_2_out, Iniciar_out);
  DipSwitch dipswitch_1 (.out(dipswitch_1_out[0]));
  DipSwitch dipswitch_2 (.out(dipswitch_1_out[1]));
  assign not_3_out = ~B0_out;  // Not not_3, 7 bits wide
  DipSwitch Dificuldade (.out(Dificuldade_out));
  bitbakery #(.applicationType("IVERILOG"), .CodeFile("/home/thaylor/Projects/BitBakery/verilog/simulacao/digital_verilog.v")) u_bitbakery (
    .clock_in(clk), .reset_in(not_1_out), .iniciar_in(not_2_out), .dificuldade(Dificuldade_out),
    .minigame(dipswitch_1_out), .botoes_in(not_3_out), .echo(u_mock_hcsr04_echo), .saida_serial(Serial),
    .pwm(Pwm), .trigger(u_bitbakery_trigger), .pontuacao_out(Pontuacao), .db_estado(Estado),
    .db_minigame(db_Minigame), .db_jogada(u_bitbakery_db_jogada), .db_iniciar(db_iniciar),
    .db_player_position(u_bitbakery_db_player_position), .db_map_obstacle(u_bitbakery_db_map_obstacle));  // open: db_clock, db_map_objective
  mock_hcsr04 #(.applicationType("IVERILOG")) u_mock_hcsr04 (
    .clock(clk), .reset(not_1_out), .trigger(u_bitbakery_trigger), .distancia(Distancia),
    .echo(u_mock_hcsr04_echo));
  LED L0 (.in(u_bitbakery_db_jogada[0]));
  LED L1 (.in(u_bitbakery_db_jogada[1]));
  LED L2 (.in(u_bitbakery_db_jogada[2]));
  LED L3 (.in(u_bitbakery_db_jogada[3]));
  LED L4 (.in(u_bitbakery_db_jogada[4]));
  LED L5 (.in(u_bitbakery_db_jogada[5]));
  LED L6 (.in(u_bitbakery_db_jogada[6]));
  LED led_1 (.in(u_bitbakery_db_player_position[0]));
  LED led_2 (.in(u_bitbakery_db_player_position[1]));
  LED led_3 (.in(u_bitbakery_db_player_position[2]));
  LED led_4 (.in(u_bitbakery_db_player_position[3]));
  LED led_5 (.in(u_bitbakery_db_map_obstacle[0]));
  LED led_6 (.in(u_bitbakery_db_map_obstacle[1]));
  LED led_7 (.in(u_bitbakery_db_map_obstacle[4]));
  LED led_8 (.in(u_bitbakery_db_map_obstacle[5]));
  LED led_9 (.in(u_bitbakery_db_map_obstacle[8]));
  LED led_10 (.in(u_bitbakery_db_map_obstacle[9]));
  LED led_11 (.in(u_bitbakery_db_map_obstacle[12]));
  LED led_12 (.in(u_bitbakery_db_map_obstacle[13]));
  LED led_13 (.in(u_bitbakery_db_map_obstacle[16]));
  LED led_14 (.in(u_bitbakery_db_map_obstacle[17]));
  LED led_15 (.in(u_bitbakery_db_map_obstacle[20]));
  LED led_16 (.in(u_bitbakery_db_map_obstacle[21]));
  LED led_17 (.in(u_bitbakery_db_map_obstacle[24]));
  LED led_18 (.in(u_bitbakery_db_map_obstacle[25]));
  LED led_19 (.in(u_bitbakery_db_map_obstacle[28]));
  LED led_20 (.in(u_bitbakery_db_map_obstacle[29]));
  LED led_21 (.in(u_bitbakery_db_map_obstacle[32]));
  LED led_22 (.in(u_bitbakery_db_map_obstacle[33]));
  LED led_23 (.in(u_bitbakery_db_map_obstacle[36]));
  LED led_24 (.in(u_bitbakery_db_map_obstacle[37]));
  LED led_25 (.in(u_bitbakery_db_map_obstacle[40]));
  LED led_26 (.in(u_bitbakery_db_map_obstacle[41]));
  LED led_27 (.in(u_bitbakery_db_map_obstacle[44]));
  LED led_28 (.in(u_bitbakery_db_map_obstacle[45]));
  LED led_29 (.in(u_bitbakery_db_map_obstacle[48]));
  LED led_30 (.in(u_bitbakery_db_map_obstacle[49]));
  LED led_31 (.in(u_bitbakery_db_map_obstacle[52]));
  LED led_32 (.in(u_bitbakery_db_map_obstacle[53]));
  LED led_33 (.in(u_bitbakery_db_map_obstacle[56]));
  LED led_34 (.in(u_bitbakery_db_map_obstacle[57]));
  LED led_35 (.in(u_bitbakery_db_map_obstacle[60]));
  LED led_36 (.in(u_bitbakery_db_map_obstacle[61]));
  LED led_37 (.in(u_bitbakery_db_map_obstacle[2]));
  LED led_38 (.in(u_bitbakery_db_map_obstacle[3]));
  LED led_39 (.in(u_bitbakery_db_map_obstacle[6]));
  LED led_40 (.in(u_bitbakery_db_map_obstacle[7]));
  LED led_41 (.in(u_bitbakery_db_map_obstacle[10]));
  LED led_42 (.in(u_bitbakery_db_map_obstacle[11]));
  LED led_43 (.in(u_bitbakery_db_map_obstacle[14]));
  LED led_44 (.in(u_bitbakery_db_map_obstacle[15]));
  LED led_45 (.in(u_bitbakery_db_map_obstacle[18]));
  LED led_46 (.in(u_bitbakery_db_map_obstacle[19]));
  LED led_47 (.in(u_bitbakery_db_map_obstacle[22]));
  LED led_48 (.in(u_bitbakery_db_map_obstacle[23]));
  LED led_49 (.in(u_bitbakery_db_map_obstacle[26]));
  LED led_50 (.in(u_bitbakery_db_map_obstacle[27]));
  LED led_51 (.in(u_bitbakery_db_map_obstacle[30]));
  LED led_52 (.in(u_bitbakery_db_map_obstacle[31]));
  LED led_53 (.in(u_bitbakery_db_map_obstacle[34]));
  LED led_54 (.in(u_bitbakery_db_map_obstacle[35]));
  LED led_55 (.in(u_bitbakery_db_map_obstacle[38]));
  LED led_56 (.in(u_bitbakery_db_map_obstacle[39]));
  LED led_57 (.in(u_bitbakery_db_map_obstacle[42]));
  LED led_58 (.in(u_bitbakery_db_map_obstacle[43]));
  LED led_59 (.in(u_bitbakery_db_map_obstacle[46]));
  LED led_60 (.in(u_bitbakery_db_map_obstacle[47]));
  LED led_61 (.in(u_bitbakery_db_map_obstacle[50]));
  LED led_62 (.in(u_bitbakery_db_map_obstacle[51]));
  LED led_63 (.in(u_bitbakery_db_map_obstacle[54]));
  LED led_64 (.in(u_bitbakery_db_map_obstacle[55]));
  LED led_65 (.in(u_bitbakery_db_map_obstacle[58]));
  LED led_66 (.in(u_bitbakery_db_map_obstacle[59]));
  LED led_67 (.in(u_bitbakery_db_map_obstacle[62]));
  LED led_68 (.in(u_bitbakery_db_map_obstacle[63]));

  // Notes on the sheet:
  //   clk: Hz: 50000000
endmodule

/* Code of mock_hcsr04:
module mock_hcsr04 (
    input wire clock,           // Clock de 1MHz (periodo de 1us) para timing correto
    input wire reset,
    input wire trigger,         // Pulso de trigger do controlador
    input wire [1:0] distancia, // Distancia simulada (00=1cm, 01=6cm, 10=10cm, 11=14cm)
    output reg echo             // Pulso de echo para o controlador
);

// Estados da maquina de estados
localparam IDLE         = 3'd0;
localparam WAIT_TRIGGER = 3'd1;
localparam DELAY        = 3'd2;
localparam ECHO_PULSE   = 3'd3;

// Registradores
reg [2:0] estado;
reg [11:0] contador;
reg [11:0] echo_duration;

// Duracao do echo em microsegundos baseada na distancia
// 58us por cm (ida e volta do som)
wire [11:0] duracao_1cm  = 12'd58;   //  1cm
wire [11:0] duracao_6cm  = 12'd348;  //  6cm (58*6)
wire [11:0] duracao_10cm = 12'd580;  // 10cm (58*10)
wire [11:0] duracao_14cm = 12'd812;  // 14cm (58*14)

// Delay antes do echo (tempo de processamento do sensor)
localparam SENSOR_DELAY = 12'd150;   // 150us de delay

// Inicializacao
initial begin
    estado = IDLE;
    echo = 1'b0;
    contador = 12'd0;
    echo_duration = duracao_1cm;
end

// Selecao da duracao do echo baseada na distancia
always @(*) begin
    case (distancia)
        2'b00: echo_duration = duracao_1cm;
        2'b01: echo_duration = duracao_6cm;
        2'b10: echo_duration = duracao_10cm;
        2'b11: echo_duration = duracao_14cm;
        default: echo_duration = duracao_1cm;
    endcase
end

// Maquina de estados
always @(posedge clock or posedge reset) begin
    if (reset) begin
        estado <= IDLE;
        echo <= 1'b0;
        contador <= 12'd0;
    end
    else begin
        case (estado)
            IDLE: begin
                echo <= 1'b0;
                contador <= 12'd0;
                if (trigger) begin
                    estado <= WAIT_TRIGGER;
                end
            end
            
            WAIT_TRIGGER: begin
                // Espera o trigger cair
                if (!trigger) begin
                    estado <= DELAY;
                    contador <= 12'd0;
                end
            end
            
            DELAY: begin
                // Simula o delay do sensor (150us)
                if (contador < SENSOR_DELAY) begin
                    contador <= contador + 1'b1;
                end
                else begin
                    estado <= ECHO_PULSE;
                    contador <= 12'd0;
                    echo <= 1'b1;
                end
            end
            
            ECHO_PULSE: begin
                // Gera o pulso de echo com duracao proporcional a distancia
                if (contador < echo_duration) begin
                    contador <= contador + 1'b1;
                    echo <= 1'b1;
                end
                else begin
                    echo <= 1'b0;
                    estado <= IDLE;
                    contador <= 12'd0;
                end
            end
            
            default: begin
                estado <= IDLE;
                echo <= 1'b0;
                contador <= 12'd0;
            end
        endcase
    end
end

endmodule
*/
